// Logisim project odvdn06.circ as structural Verilog: 1 circuit, main circuit main
module main (
  input  x1,
  input  x2,
  input  x3,
  input  x4,
  output out_5
);

  wire and_1_out, and_2_out, and_3_out, and_4_out, and_5_out, and_6_out, and_7_out, and_8_out, nor_1_out,
       not_1_out, not_2_out, not_3_out, not_4_out, not_5_out, or_1_out, or_2_out, or_3_out, or_4_out,
       xor_1_out, xor_2_out, xor_3_out;

  not not_1 (not_1_out, x1);
  not not_2 (not_2_out, x2);
  not not_3 (not_3_out, x3);
  not not_4 (not_4_out, x4);
  ExactlyOne xor_1 (.out(xor_1_out), .in0(x1), .in1(x2), .in2(x3), .in3(x4));
  nor nor_1 (nor_1_out, x1, x2, x3, x4);
  or or_1 (or_1_out, xor_1_out, nor_1_out);
  ExactlyOne xor_2 (.out(xor_2_out), .in0(not_1_out), .in1(x2), .in2(not_3_out), .in3(x4));
  and and_1 (and_1_out, not_1_out, not_3_out, not_4_out, not_2_out);
  and and_2 (and_2_out, not_1_out, x2, not_4_out, x3);
  and and_3 (and_3_out, not_1_out, x2, not_3_out, x4);
  and and_4 (and_4_out, not_2_out, x1, not_4_out, x3);
  and and_5 (and_5_out, not_2_out, x1, not_3_out, x4);
  and and_6 (and_6_out, x3, x1, x2, x4);
  xor xor_3 (xor_3_out, x1, x4);
  or or_2 (or_2_out, not_1_out, not_3_out);
  not not_5 (not_5_out, xor_3_out);
  or or_3 (or_3_out, or_1_out, xor_2_out);
  or or_4 (or_4_out, and_1_out, and_2_out, and_3_out, and_4_out, and_5_out, and_6_out);
  and and_7 (and_7_out, or_2_out, or_4_out);
  and and_8 (and_8_out, not_5_out, or_3_out);
  or or_5 (out_5, and_8_out, and_7_out);
endmodule
