// Logisim project odvdn07.circ as structural Verilog: 1 circuit, main circuit main
module main (
  input  x1,
  input  x2,
  input  x3,
  input  x4,
  output f
);

  wire multiplexer_1_out, multiplexer_2_out, not_1_out, not_2_out, not_3_out, not_4_out;

  not not_1 (not_1_out, x1);
  not not_2 (not_2_out, x2);
  not not_3 (not_3_out, x3);
  not not_4 (not_4_out, x4);
  Multiplexer multiplexer_1 (.in0(1'b1), .in1(multiplexer_2_out), .out(multiplexer_1_out), .sel(x4));
  Multiplexer multiplexer_2 (.in0(not_3_out), .in1(x3), .out(multiplexer_2_out), .sel(x2));
  Multiplexer multiplexer_3 (.in0(multiplexer_1_out), .in1(multiplexer_2_out), .out(f), .sel(x1));
endmodule
