// Logisim project odvdn08.circ as structural Verilog: 2 circuits, main circuit main
module main (
  input  x1,
  input  x2,
  input  x3,
  input  x4
);

  wire and_1_out, clock_1_out, pomozno_1_out_5, s_r_ff_1_q, t_ff_1_q, xor_1_out;

  xor xor_1 (xor_1_out, x2, t_ff_1_q);
  and and_1 (and_1_out, x2, x3);
  Clock clock_1 (.out(clock_1_out));
  T_Flip_Flop t_ff_1 (.T(pomozno_1_out_5), .clk(clock_1_out), .Q(t_ff_1_q));  // open: Qn, reset, preset
  pomozno pomozno_1 (.x1(x1), .x2(x2), .q1(t_ff_1_q), .q2(s_r_ff_1_q), .out_5(pomozno_1_out_5));
  S_R_Flip_Flop s_r_ff_1 (.S(xor_1_out), .R(and_1_out), .clk(clock_1_out), .Q(s_r_ff_1_q));  // open: reset, Qn, preset

  // Notes on the sheet:
  //   q1
endmodule

module pomozno (
  input  x1,
  input  x2,
  input  q1,
  input  q2,
  output out_5
);

  wire not_1_out, not_2_out;

  not not_1 (not_1_out, q2);
  not not_2 (not_2_out, x2);
  Multiplexer #(.select(2)) multiplexer_1 (
    .in0(not_1_out), .in1(not_2_out), .in2(q2), .in3(1'b0), .out(out_5), .sel({x1, q1}));
endmodule
